# Fritzing sketch arriere (saved by Fritzing 1.0.0rc)
perfboards: 1

parts:
  JP1 = Header 10 [package=1x10-2mm-smd]  # not connected
  U1 = AD22100 - Voltage Output Temperature Sensor with Signal Conditioning [part_number=AD22100]  # not connected
  JP2 = Header 10 [package=1x10-2mm-smd]  # not connected
  BAT1 = Battery Holders [package=battery-aaa]
  VCC1 = Battery

nets:
  N1: BAT1.-, VCC1.-
